# Fritzing sketch Saci Fermentation Control - V2 (saved by Fritzing 0.9.2b)
circuit board: 7.2cm x 6cm
breadboards: 1

parts:
  Q1 = NPN-Transistor [package="TO92 [THT]"]
  Q2 = NPN-Transistor [package="TO92 [THT]"]
  D1 = Schottky Diode [part_number=1N5817 package="300 mil [THT]"]
  D2 = Schottky Diode [part_number=1N5817 package="300 mil [THT]"]
  Componente2 = Relay T73
  J1 = female pin header, 15 pins [form="♀ (female)"]
  J2 = female pin header, 15 pins [form="♀ (female)"]
  R1 = Resistor [tolerance=±5% resistance=4.7 package=THT]
  J4 = screw terminal, 2 pins
  J3 = screw terminal, 2 pins
  Componente1 = Relay T73
  J5 = screw terminal, 3 pins
  J6 = screw terminal, 3 pins

nets:
  N1: Q1.E, J1.pin7
  N2: Q1.B, J1.pin10
  N3: Q1.C, D2.anode, Componente1.C2
  N4: Q2.E, J1.pin14, J5.pin2
  N5: Q2.B, J1.pin11
  N6: Q2.C, D1.anode, Componente2.C2
  N7: D1.cathode, D2.cathode, Componente2.C1, J2.pin3, R1.Pin_0, Componente1.C1, J5.pin3
  N8: Componente2.COM, J4.pin1, J3.pin1, Componente1.COM
  N9: Componente2.NO, J3.pin2
  N10: J1.pin3, R1.Pin_1, J5.pin1
  N11: J4.pin2, Componente1.NO
  N12: J6.pin1, J6.pin2, J6.pin3

custom parts:
  Relay T73: An T73 Mini PCB Relay
